# Fritzing sketch Captive Portal_ESP32_LED_Matrix (saved by Fritzing 0.9.3b)
breadboards: 2

parts:
  U1 = ESP32-38PinWide [part_number=ESP32-38PinWide]
  U2 = WS2812 RGB LED matrix 8x8

nets:
  N1: U1.GPIO17, U2.DIN
  GND: U1.GND, U2.GND

custom parts:
  ESP32-38PinWide: Generic 38-Pin ESP32 with wide format (only access to one side of pins on a breadboard) based on Stephen Lilley's HiLetgo ESP-WROOM-32 ESP32 ESP-32S Development Board.
  WS2812 RGB LED matrix 8x8: WS2812 matrix 8x8
